# Fritzing sketch joystick (saved by Fritzing 0.9.3b)

parts:
  Componente1 = Thumb Joystick
  Componente2 = Arduino Uno (Rev3)

nets:
  GND: Componente1.GND, Componente2.GND
  N1: Componente1.SEL, Componente2.D2
  N2: Componente1.HORZ, Componente2.A0
  N3: Componente1.VERT, Componente2.A1
  VCC: Componente1.VCC, Componente2.5V
